# Fritzing sketch BT Voice Controlled LED (saved by Fritzing 0.9.3b)
breadboards: 1

parts:
  Part1 = Bluetooth HC-05 Macho
  Part2 = Arduino Uno (Rev3)
  LED1 = LED - 5mm [color="Red (633nm)" package="5 mm [THT]"]

nets:
  N1: Part1.TXD, Part2.D10_PWM/SS
  N2: Part1.RXD, Part2.D11_PWM/MOSI
  VCC: Part1.VCC, Part2.5V
  GND: Part1.GND, Part2.GND, LED1.cathode
  N3: Part2.D13/SCK, LED1.anode

// code stored in the sketch: Voice Controlled BT LED.ino
//Works in conjunction with the AMR_Voice app for Android
#include <SoftwareSerial.h>
SoftwareSerial myserial(10, 11); // RX, TX

String voice;
int led5 = 13; //Connect LED 5 To Pin #13 

void setup() {
  Serial.begin(9600);
  myserial.begin(9600);
  pinMode(led5, OUTPUT);
}
  
void loop() {
  while (myserial.available()){  //Check if there is an available byte to read
    delay(10); //Delay added to make thing stable 
    char c = myserial.read(); //Conduct a serial read
    if (c == '#') {
      break;
    } //Exit the loop when the # is detected after the word
    voice += c; //Shorthand for voice = voice + c
  }  
  if (voice.length() > 0) {
    Serial.println(voice); 
    if(voice == "*on") {
      digitalWrite(led5, HIGH);
    }
    else if(voice == "*off") {
      digitalWrite(led5, LOW);
    }
//-----------------------------------------------------------------------//  
voice="";}} //Reset the variable after initiating
