# Fritzing sketch Basic Ultrasonic Distance (saved by Fritzing 0.9.3b)
breadboards: 1

parts:
  Part1 = Arduino Uno (Rev3)
  hc-sr1 = hc-sr04

nets:
  N1: Part1.D8, hc-sr1.Echo
  N2: Part1.D9_PWM, hc-sr1.Trig
  5V: Part1.5V, hc-sr1.VCC
  GND: Part1.GND, hc-sr1.GND

// code stored in the sketch: Basic Ultrasonic Distance.ino
#define trigPin 9
#define echoPin 8

void setup() {
  // put your setup code here, to run once:
  Serial.begin(9600);
  pinMode(trigPin,OUTPUT);
  pinMode(echoPin,INPUT);
}

void loop() {
  // put your main code here, to run repeatedly:
  long duration, distance;
  digitalWrite(trigPin, LOW);
  delayMicroseconds(2);
  digitalWrite(trigPin, HIGH);
  delayMicroseconds(10);
  digitalWrite(trigPin, LOW);
  duration = pulseIn(echoPin, HIGH);
  distance = (duration/2) / 29.1;
  Serial.println(distance);
  delay(500);
}
