# Fritzing sketch Continually Changing RGB LED (saved by Fritzing 0.9.3b)
circuit board: 8.46667cm x 5.64444cm
breadboards: 1

parts:
  Part1 = Arduino Uno (Rev3)
  LED1 = RGB LED (com. anode, rbg) [package="5 mm [THT]"]
  R1 = Resistor [tolerance=±5% resistance=220 package=THT]

nets:
  N1: Part1.D11_PWM/MOSI, LED1.red_cathode
  N2: Part1.D12/MISO, LED1.blue_cathode
  N3: Part1.D13/SCK, LED1.green_cathode
  N4: Part1.5V, R1.Pin_1
  N5: LED1.common_anode, R1.Pin_0

// code stored in the sketch: Continually Changing RGB LED.ino
int redPin = 11;
int greenPin = 12;
int bluePin = 13;

void setup() {
  pinMode(redPin, OUTPUT);
  pinMode(greenPin, OUTPUT);
  pinMode(bluePin, OUTPUT);
}

void loop() {
  // put your main code here, to run repeatedly:
  int redColor = random(256);
  int blueColor = random(256);
  int greenColor = random(256);
  analogWrite(redPin,redColor);
  analogWrite(bluePin,blueColor);
  analogWrite(greenPin,greenColor);
  delay(1000);
}
