# Fritzing sketch Voice Controlled RGB (saved by Fritzing 0.9.3b)
breadboards: 1

parts:
  Part2 = Arduino Uno (Rev3)
  Part3 = Bluetooth HC-05 Macho
  LED2 = RGB LED (com. anode, rbg) [package="5 mm [THT]"]
  R1 = Resistor [tolerance=±5% resistance=220 package=THT]

nets (from the breadboard view):
  N1: Part2.D10_PWM/SS, Part3.RXD
  N2: Part2.D11_PWM/MOSI, Part3.TXD
  GND: Part2.GND, Part3.GND
  N3: Part2.D3_PWM, LED2.green_cathode
  N4: Part2.D5_PWM, LED2.blue_cathode
  N5: Part2.D6_PWM, LED2.red_cathode
  5V: Part2.5V, Part3.VCC, R1.Pin_0
  N6: LED2.common_anode, R1.Pin_1

// code stored in the sketch: Voice Controlled RGB.ino
#include <SoftwareSerial.h>
SoftwareSerial myserial(10,11); //RX, TX

String voice;
int red = 6;
int green = 5;
int blue = 3;
#define COMMON_ANODE
void setup() {
  // put your setup code here, to run once:
  Serial.begin(9600);
  myserial.begin(9600);
  pinMode(red,OUTPUT);
  pinMode(blue,OUTPUT);
  pinMode(green,OUTPUT);
  digitalWrite(red,HIGH);
  digitalWrite(blue,HIGH);
  digitalWrite(green,HIGH);
}

void loop() {

  // put your main code here, to run repeatedly:
  while (myserial.available()){  //Check if there is an available byte to read
      delay(10); //Delay added to make thing stable 
      char c = myserial.read(); //Conduct a serial read
      if (c == '#') {
        break;
      } //Exit the loop when the # is detected after the word
      voice += c; //Shorthand for voice = voice + c
    }  
    if (voice.length() > 0) {
      Serial.println(voice);
      if(voice=="*blue"){
        setColor(255,0,0);
      }
      else if(voice=="*red"){
        setColor(0,255,0);
      }
      else if(voice=="*green"){
        setColor(0,0,255);
      }
      else if(voice=="*strobe"){
        for (int i=0;i<10;i++){
          digitalWrite(red,LOW);
          digitalWrite(blue,LOW);
          digitalWrite(green,LOW);
          delay(100);
          digitalWrite(red,HIGH);
          digitalWrite(blue,HIGH);
          digitalWrite(green,HIGH);
          delay(100);
        }
      }
      else if(voice=="*random"){
        int rr = random(255);
        int rb = random(255);
        int rg = random(255);
        setColor(rr,rg,rb);
      }
      else if(voice=="*off"){
        digitalWrite(red,HIGH);
        digitalWrite(blue,HIGH);
        digitalWrite(green,HIGH);
      }
      voice="";
    } 
}

void setColor(int blueI, int redI, int greenI){
  #ifdef COMMON_ANODE
    redI = 255 - redI;
    greenI = 255 - greenI;
    blueI = 255 - blueI;
  #endif
  analogWrite(red, redI);
  analogWrite(green, greenI);
  analogWrite(blue, blueI); 
}
